// Logisim project Q1.circ as structural Verilog: 2 circuits, main circuit div
module div (
  input  [3:0] in_1,
  input  [10:0] in_2,
  output [10:0] out_3
);

  wire [3:0] O1, xor_1_out;

  Multiplexer #(.width(4), .enable("false")) multiplexer_1 (.in0(4'b0000), .in1(in_1), .out(O1), .sel(in_2[10]));
  assign xor_1_out = in_2[10:7] ^ O1;  // XOR_Gate xor_1, 4 bits wide
  Shifter #(.width(11)) shifter_1 (.in({xor_1_out, in_2[6:0]}), .\dist (4'b0001), .out(out_3));

  // Other names for the same wires on the sheet: B[3:0] = in_1; I1 = in_2[10]
endmodule

module CRC (
  input  [7:0] in_1,
  input  [3:0] in_2,
  output [10:0] out_3
);

  wire [7:0] div_8_out_3;
  wire [10:0] div_1_out_3, div_2_out_3, div_3_out_3, div_4_out_3, div_5_out_3, div_6_out_3, div_7_out_3;

  div div_1 (.in_1(in_2), .in_2({in_1, 3'b000}), .out_3(div_1_out_3));
  div div_2 (.in_1(in_2), .in_2(div_1_out_3), .out_3(div_2_out_3));
  // Probe on div_1_out_3
  // Probe on div_2_out_3
  div div_3 (.in_1(in_2), .in_2(div_2_out_3), .out_3(div_3_out_3));
  // Probe on div_3_out_3
  div div_4 (.in_1(in_2), .in_2(div_3_out_3), .out_3(div_4_out_3));
  div div_5 (.in_1(in_2), .in_2(div_4_out_3), .out_3(div_5_out_3));
  div div_6 (.in_1(in_2), .in_2(div_5_out_3), .out_3(div_6_out_3));
  div div_7 (.in_1(in_2), .in_2(div_6_out_3), .out_3(div_7_out_3));
  div div_8 (.in_1(in_2), .in_2(div_7_out_3), .out_3({out_3[2:0], div_8_out_3}));

  assign out_3[10:3] = in_1;

  // Other names for the same wires on the sheet: B[3:0] = in_2; A[7:0] = in_1
endmodule
