// Logisim project Q4.circ as structural Verilog: 2 circuits, main circuit fsm
module fsm (
  input  in_1,
  input  [1:0] in_2,
  output out_3
);

  wire clock_1_out, s1, s2;
  wire [1:0] ans, multiplexer_1_out;

  fsm_cir fsm_cir_1 (.s1(s1), .s2(s2), .i1(in_2[1]), .i2(in_2[0]), .t1(ans[0]), .t2(ans[1]));
  Multiplexer #(.width(2), .enable("false")) multiplexer_1 (
    .in0(ans), .in1(2'b00), .out(multiplexer_1_out), .sel(in_1));
  and and_1 (out_3, ans[0], ans[1]);
  Register #(.width(2)) register_1 (.D(multiplexer_1_out), .Q({s2, s1}), .clk(clock_1_out));  // open: en, clr
  Clock clock_1 (.out(clock_1_out));

  // Other names for the same wires on the sheet: i2 = in_2[0]; i1 = in_2[1]; reset = in_1
endmodule

module fsm_cir (
  input  s1,
  input  s2,
  input  i1,
  input  i2,
  output t1,
  output t2
);

  wire and_1_out, and_2_out, and_3_out, and_4_out, not_1_out, not_2_out, not_3_out, not_4_out, not_5_out,
       not_6_out, not_7_out;

  not not_1 (not_1_out, s1);
  and and_1 (and_1_out, not_1_out, s2, not_2_out);
  not not_2 (not_2_out, i2);
  not not_3 (not_3_out, s2);
  and and_2 (and_2_out, s1, not_3_out, not_4_out);
  not not_4 (not_4_out, i2);
  not not_5 (not_5_out, i1);
  and and_3 (and_3_out, not_5_out, i2);
  not not_6 (not_6_out, s2);
  and and_4 (and_4_out, s1, not_6_out, not_7_out);
  not not_7 (not_7_out, i2);
  or or_1 (t1, and_1_out, and_2_out);
  or or_2 (t2, and_3_out, and_4_out);
endmodule
