// Logisim project CPU-j.circ as structural Verilog: 7 circuits, main circuit alu
module main (
  input  in_1,
  output [31:0] Instr,
  output RegWrite,
  output [4:0] RegAddr,
  output [31:0] RegData,
  output MemWrite,
  output [4:0] MemAddr,
  output [31:0] MemData
);

  wire aluB, and_1_out, clk, if_jump_to_label_out, ifBeq, ifJ, neqz, not_1_out, regSlt, toReg;
  wire [1:0] aluOp, extOp;
  wire [4:0] rd, rs, rt;
  wire [15:0] imm;
  wire [31:0] ALUres, dm_1_out, ext_1_output, grf_1_o1, multiplexer_2_out;

  Clock clock_1 (.out(clk));
  not not_1 (not_1_out, neqz);
  and and_1 (and_1_out, not_1_out, ifBeq);
  buf if_jump_to_label (if_jump_to_label_out, and_1_out);  // OR_Gate
  Multiplexer #(.width(5), .enable("false")) multiplexer_1 (.in0(rt), .in1(rd), .out(RegAddr), .sel(regSlt));
  IFU ifu_1 (.in_1(if_jump_to_label_out), .in_2(ifJ), .in_3(in_1), .in_4(clk), .out_5(Instr));
  controller controller_1 (
    .instr(Instr), .regSlt(regSlt), .regWE(RegWrite), .dmWE(MemWrite), .extOp(extOp), .aluOp(aluOp),
    .aluB(aluB), .toReg(toReg), .ifBeq(ifBeq), .rs(rs), .rt(rt), .rd(rd), .imm(imm), .out_15(ifJ));  // open: 神秘金币
  grf grf_1 (
    .A1(rs), .A2(rt), .A3(RegAddr), .data(RegData), .clk(clk), .reset(in_1), .we(RegWrite), .O1(grf_1_o1),
    .O2(MemData));
  EXT ext_1 (.\input (imm), .sel_00_0ext_01_signext_10_ext___0_2__11_toHigh16(extOp), .\output (ext_1_output));
  Multiplexer #(.width(32), .enable("false")) multiplexer_2 (
    .in0(MemData), .in1(ext_1_output), .out(multiplexer_2_out), .sel(aluB));
  alu alu_1 (
    .A(grf_1_o1), .B(multiplexer_2_out), .sel_00__01__10__11(aluOp),
    .C({ALUres[31:7], MemAddr, ALUres[1:0]}), .notzero(neqz));
  // Probe on Instr
  DM dm_1 (.address(MemAddr), .data(MemData), .WE(MemWrite), .clk(clk), .reset(in_1), .out(dm_1_out));
  Multiplexer #(.width(32), .enable("false")) multiplexer_3 (
    .in0(dm_1_out), .in1({ALUres[31:7], MemAddr, ALUres[1:0]}), .out(RegData), .sel(toReg));

  // Other names for the same wires on the sheet: ALUres[6:2] = MemAddr; Data[31:0] = RegData; dmWE = MemWrite;
  //   readRt[31:0] = MemData; regWE = RegWrite; reset = in_1
endmodule

// ALU
module alu (
  input  [31:0] A,
  input  [31:0] B,
  input  [1:0] sel_00__01__10__11,
  output [31:0] C,
  output notzero
);

  wire [31:0] adder_1_out, and_1_out, or_1_out, subtractor_1_out;

  Adder #(.width(32)) adder_1 (.a(A), .b(B), .out(adder_1_out));  // open: cin, cout
  Subtractor #(.width(32)) subtractor_1 (.a(A), .b(B), .out(subtractor_1_out));  // open: bin, bout
  assign and_1_out = A & B;  // AND_Gate and_1, 32 bits wide
  assign or_1_out = A | B;  // OR_Gate or_1, 32 bits wide
  Multiplexer #(.select(2), .width(32), .enable("false")) multiplexer_1 (
    .in0(adder_1_out), .in1(subtractor_1_out), .in2(and_1_out), .in3(or_1_out), .out(C),
    .sel(sel_00__01__10__11));
  or or_2 (notzero, C[0], C[1], C[2], C[3], C[4], C[5], C[6], C[7], C[8], C[9], C[10], C[11], C[12], C[13], C[14], C[15], C[17], C[18], C[19], C[20], C[21], C[22], C[23], C[24], C[25], C[26], C[27], C[28], C[29], C[30], C[31]);
endmodule

// GRF
module grf (
  input  clk,
  input  reset,
  input  we,
  input  [4:0] A1,
  input  [4:0] A2,
  input  [4:0] A3,
  input  [31:0] data,
  output [31:0] O1,
  output [31:0] O2
);

  wire o300, o301, o302, o303, o304, o305, o306, o307, o308, o309, o310, o311, o312, o313, o314, o315, o316,
       o317, o318, o319, o320, o321, o322, o323, o324, o325, o326, o327, o328, o329, o330, o331;
  wire [31:0] o00, o01, o02, o03, o04, o05, o06, o07, o08, o09, o10, o11, o12, o13, o14, o15, o16, o17, o18,
       o19, o20, o21, o22, o23, o24, o25, o26, o27, o28, o29, o30, o31;

  Demultiplexer #(.select(5), .enable("false")) demultiplexer_1 (
    .out0(o300), .out1(o301), .out2(o302), .out3(o303), .out4(o304), .out5(o305), .out6(o306), .out7(o307),
    .out8(o308), .out9(o309), .out10(o310), .out11(o311), .out12(o312), .out13(o313), .out14(o314),
    .out15(o315), .out16(o316), .out17(o317), .out18(o318), .out19(o319), .out20(o320), .out21(o321),
    .out22(o322), .out23(o323), .out24(o324), .out25(o325), .out26(o326), .out27(o327), .out28(o328),
    .out29(o329), .out30(o330), .out31(o331), .in(we), .sel(A3));
  Register #(.width(32)) register_1 (.D({32{1'b0}}), .en(o300), .Q(o00), .clk(clk), .clr(reset));
  Register #(.width(32)) register_2 (.D(data), .en(o308), .Q(o08), .clk(clk), .clr(reset));
  Register #(.width(32)) register_3 (.D(data), .en(o316), .Q(o16), .clk(clk), .clr(reset));
  Register #(.width(32)) register_4 (.D(data), .en(o324), .Q(o24), .clk(clk), .clr(reset));
  Register #(.width(32)) register_5 (.D(data), .en(o301), .Q(o01), .clk(clk), .clr(reset));
  Register #(.width(32)) register_6 (.D(data), .en(o309), .Q(o09), .clk(clk), .clr(reset));
  Register #(.width(32)) register_7 (.D(data), .en(o317), .Q(o17), .clk(clk), .clr(reset));
  Register #(.width(32)) register_8 (.D(data), .en(o325), .Q(o25), .clk(clk), .clr(reset));
  Register #(.width(32)) register_9 (.D(data), .en(o302), .Q(o02), .clk(clk), .clr(reset));
  Register #(.width(32)) register_10 (.D(data), .en(o310), .Q(o10), .clk(clk), .clr(reset));
  Register #(.width(32)) register_11 (.D(data), .en(o318), .Q(o18), .clk(clk), .clr(reset));
  Register #(.width(32)) register_12 (.D(data), .en(o326), .Q(o26), .clk(clk), .clr(reset));
  Multiplexer #(.select(5), .width(32), .enable("false")) multiplexer_1 (
    .in0(o00), .in1(o01), .in2(o02), .in3(o03), .in4(o04), .in5(o05), .in6(o06), .in7(o07), .in8(o08),
    .in9(o09), .in10(o10), .in11(o11), .in12(o12), .in13(o13), .in14(o14), .in15(o15), .in16(o16),
    .in17(o17), .in18(o18), .in19(o19), .in20(o20), .in21(o21), .in22(o22), .in23(o23), .in24(o24),
    .in25(o25), .in26(o26), .in27(o27), .in28(o28), .in29(o29), .in30(o30), .in31(o31), .out(O1), .sel(A1));
  Register #(.width(32)) register_13 (.D(data), .en(o303), .Q(o03), .clk(clk), .clr(reset));
  Register #(.width(32)) register_14 (.D(data), .en(o311), .Q(o11), .clk(clk), .clr(reset));
  Register #(.width(32)) register_15 (.D(data), .en(o319), .Q(o19), .clk(clk), .clr(reset));
  Register #(.width(32)) register_16 (.D(data), .en(o327), .Q(o27), .clk(clk), .clr(reset));
  Register #(.width(32)) register_17 (.D(data), .en(o304), .Q(o04), .clk(clk), .clr(reset));
  Register #(.width(32)) register_18 (.D(data), .en(o312), .Q(o12), .clk(clk), .clr(reset));
  Register #(.width(32)) register_19 (.D(data), .en(o320), .Q(o20), .clk(clk), .clr(reset));
  Register #(.width(32)) register_20 (.D(data), .en(o328), .Q(o28), .clk(clk), .clr(reset));
  Register #(.width(32)) register_21 (.D(data), .en(o305), .Q(o05), .clk(clk), .clr(reset));
  Register #(.width(32)) register_22 (.D(data), .en(o313), .Q(o13), .clk(clk), .clr(reset));
  Register #(.width(32)) register_23 (.D(data), .en(o321), .Q(o21), .clk(clk), .clr(reset));
  Register #(.width(32)) register_24 (.D(data), .en(o329), .Q(o29), .clk(clk), .clr(reset));
  Multiplexer #(.select(5), .width(32), .enable("false")) multiplexer_2 (
    .in0(o00), .in1(o01), .in2(o02), .in3(o03), .in4(o04), .in5(o05), .in6(o06), .in7(o07), .in8(o08),
    .in9(o09), .in10(o10), .in11(o11), .in12(o12), .in13(o13), .in14(o14), .in15(o15), .in16(o16),
    .in17(o17), .in18(o18), .in19(o19), .in20(o20), .in21(o21), .in22(o22), .in23(o23), .in24(o24),
    .in25(o25), .in26(o26), .in27(o27), .in28(o28), .in29(o29), .in30(o30), .in31(o31), .out(O2), .sel(A2));
  Register #(.width(32)) register_25 (.D(data), .en(o306), .Q(o06), .clk(clk), .clr(reset));
  Register #(.width(32)) register_26 (.D(data), .en(o314), .Q(o14), .clk(clk), .clr(reset));
  Register #(.width(32)) register_27 (.D(data), .en(o322), .Q(o22), .clk(clk), .clr(reset));
  Register #(.width(32)) register_28 (.D(data), .en(o330), .Q(o30), .clk(clk), .clr(reset));
  Register #(.width(32)) register_29 (.D(data), .en(o307), .Q(o07), .clk(clk), .clr(reset));
  Register #(.width(32)) register_30 (.D(data), .en(o315), .Q(o15), .clk(clk), .clr(reset));
  Register #(.width(32)) register_31 (.D(data), .en(o323), .Q(o23), .clk(clk), .clr(reset));
  Register #(.width(32)) register_32 (.D(data), .en(o331), .Q(o31), .clk(clk), .clr(reset));

  // Other names for the same wires on the sheet: in[31:0] = data
endmodule

module IFU (
  input  in_1,
  input  in_2,
  input  in_3,
  input  in_4,
  output [31:0] out_5
);

  wire register_1_q;
  wire [31:0] adder_1_out, adder_2_out, ext_1_output, lpc, multiplexer_1_out, multiplexer_2_out, pc;

  EXT ext_1 (.\input (out_5[15:0]), .sel_00_0ext_01_signext_10_ext___0_2__11_toHigh16(2'b10), .\output (ext_1_output));
  Multiplexer #(.width(32), .enable("false")) multiplexer_1 (
    .in0({32{1'b0}}), .in1(pc), .out(multiplexer_1_out), .sel(register_1_q));
  Register #(.width(1)) register_1 (.D(1'b1), .Q(register_1_q), .clk(in_4), .clr(in_3));  // open: en
  Multiplexer #(.width(32), .enable("false")) multiplexer_2 (
    .in0({32{1'b0}}), .in1(ext_1_output), .out(multiplexer_2_out), .sel(in_1));
  Register #(.width(32)) register_2 (.D(multiplexer_1_out), .Q(lpc), .clk(in_4), .clr(in_3));  // open: en
  Adder #(.width(32)) adder_1 (.a(lpc), .b(32'h4), .out(adder_1_out));  // open: cin, cout
  Adder #(.width(32)) adder_2 (.a(adder_1_out), .b(multiplexer_2_out), .out(adder_2_out));  // open: cin, cout
  Multiplexer #(.width(32), .enable("false")) multiplexer_3 (
    .in0(adder_2_out), .in1({lpc[31:28], out_5[25:0], 2'b00}), .out(pc), .sel(in_2));
  ROM #(.addrWidth(5), .dataWidth(32)) rom_1 (.addr(lpc[6:2]), .data(out_5));  // open: sel
  // Probe on pc

  // Other names for the same wires on the sheet: instr[31:0] = out_5; clk = in_4; ifBcom = in_1; ifJ = in_2;
  //   reset = in_3

  // Notes on the sheet:
  //   contents of rom_1 (hex, n*v repeats v):
  //   35080000 3610000a 11100011 1294823 18c6023 1130000a 8d8b0000 3c010000 34210004 1816021 1695821
  //   ad8b0000 3c010000 34210001 1214821 8000c05 3c010000 34210001 1014021 8000c02 114affff
endmodule

module EXT (
  input  [15:0] \input ,
  input  [1:0] sel_00_0ext_01_signext_10_ext___0_2__11_toHigh16,
  output [31:0] \output 
);

  Multiplexer #(.select(2), .width(32), .enable("false")) multiplexer_1 (
    .in0({{16{1'b0}}, \input }), .in1({{17{\input [15]}}, \input [14:0]}),
    .in2({{15{\input [15]}}, \input [14:0], 2'b00}), .in3({\input , {16{1'b0}}}), .out(\output ),
    .sel(sel_00_0ext_01_signext_10_ext___0_2__11_toHigh16));

  // Other names for the same wires on the sheet: sel[1:0] = sel_00_0ext_01_signext_10_ext___0_2__11_toHigh16;
  //   _2_signext[31:2] = {{15{\input [15]}}, \input [14:0]}; in[15:0] = \input ;
  //   signext[31:0] = {{17{\input [15]}}, \input [14:0]}; tohigh[31:16] = \input ; zeroext[15:0] = \input ;
  //   sign = \input [15]
endmodule

module DM (
  input  [4:0] address,
  input  [31:0] data,
  input  WE,
  input  clk,
  input  reset,
  output [31:0] out
);

  RAM #(.addrWidth(5), .dataWidth(32), .bus("separate")) ram_1 (
    .addr(address), .din(data), .data(out), .str(WE), .clk(clk), .clr(reset));  // open: sel, ld
endmodule

// CTL
module controller (
  input  [31:0] instr,
  input  \神秘金币 ,
  output regSlt,
  output regWE,
  output dmWE,
  output [1:0] extOp,
  output [1:0] aluOp,
  output aluB,
  output toReg,
  output ifBeq,
  output [4:0] rs,
  output [4:0] rt,
  output [4:0] rd,
  output [15:0] imm,
  output out_15
);

  wire addu, lui, lw, not_1_out, not_2_out, not_3_out, not_4_out, not_5_out, not_6_out, not_7_out, not_8_out,
       not_9_out, not_10_out, not_11_out, not_12_out, subu;

  not not_1 (not_1_out, instr[31]);
  not not_2 (not_2_out, instr[30]);
  not not_3 (not_3_out, instr[28]);
  not not_4 (not_4_out, instr[29]);
  not not_5 (not_5_out, instr[26]);
  not not_6 (not_6_out, instr[27]);
  not not_7 (not_7_out, instr[5]);
  not not_8 (not_8_out, instr[4]);
  not not_9 (not_9_out, instr[3]);
  not not_10 (not_10_out, instr[1]);
  not not_11 (not_11_out, instr[2]);
  not not_12 (not_12_out, instr[0]);
  and u_addu (addu, not_1_out, not_2_out, not_4_out, not_3_out, not_6_out, not_5_out, instr[5], not_8_out, not_9_out, not_11_out, not_10_out, instr[0]);
  and u_subu (subu, not_1_out, not_2_out, not_4_out, not_3_out, not_6_out, not_5_out, instr[5], not_8_out, not_9_out, not_11_out, instr[1], instr[0]);
  and ori (aluOp[1], not_1_out, not_2_out, instr[29], instr[28], not_6_out, instr[26]);
  and u_lw (lw, instr[31], not_2_out, not_4_out, not_3_out, instr[27], instr[26]);
  and sw (dmWE, instr[31], not_2_out, instr[29], not_3_out, instr[27], instr[26]);
  and u_lui (lui, not_1_out, not_2_out, instr[29], instr[28], instr[27], instr[26]);
  and beq (ifBeq, not_1_out, not_2_out, not_4_out, instr[28], not_6_out, not_5_out);
  and jcom (out_15, not_1_out, not_2_out, not_4_out, not_3_out, instr[27], not_5_out);
  or or_1 (regSlt, addu, subu);
  or or_2 (regWE, addu, subu, aluOp[1], lw, lui);
  or or_3 (toReg, addu, subu, aluOp[1], lui);
  or or_4 (aluOp[0], aluOp[1], ifBeq, subu);
  or or_5 (extOp[0], dmWE, lw, lui);
  or or_6 (extOp[1], ifBeq, lui);
  or or_7 (aluB, dmWE, lw, lui, aluOp[1]);

  assign imm = instr[15:0];
  assign rd = instr[15:11];
  assign rs = instr[25:21];
  assign rt = instr[20:16];

  // Other names for the same wires on the sheet: ori = aluOp[1]; beq = ifBeq; func[5:0] = instr[5:0];
  //   sha[4:0] = instr[10:6]; op[5:0] = instr[31:26]; jcom = out_15; sw = dmWE

  // Notes on the sheet:
  //   0:rt,1:rd
endmodule
