// Logisim project Q3 - 副本.circ as structural Verilog: 1 circuit, main circuit grf
module grf (
  input  in_1,
  input  in_2,
  input  in_3,
  input  [4:0] in_4,
  input  [4:0] in_5,
  input  [4:0] in_6,
  input  [31:0] in_7,
  output [31:0] out_8,
  output [31:0] out_9
);

  wire o300, o301, o302, o303, o304, o305, o306, o307, o308, o309, o310, o311, o312, o313, o314, o315, o316,
       o317, o318, o319, o320, o321, o322, o323, o324, o325, o326, o327, o328, o329, o330, o331;
  wire [31:0] o00, o01, o02, o03, o04, o05, o06, o07, o08, o09, o10, o11, o12, o13, o14, o15, o16, o17, o18,
       o19, o20, o21, o22, o23, o24, o25, o26, o27, o28, o29, o30, o31;

  Demultiplexer #(.select(5), .enable("false")) demultiplexer_1 (
    .out0(o300), .out1(o301), .out2(o302), .out3(o303), .out4(o304), .out5(o305), .out6(o306), .out7(o307),
    .out8(o308), .out9(o309), .out10(o310), .out11(o311), .out12(o312), .out13(o313), .out14(o314),
    .out15(o315), .out16(o316), .out17(o317), .out18(o318), .out19(o319), .out20(o320), .out21(o321),
    .out22(o322), .out23(o323), .out24(o324), .out25(o325), .out26(o326), .out27(o327), .out28(o328),
    .out29(o329), .out30(o330), .out31(o331), .in(in_3), .sel(in_6));
  Register #(.width(32)) register_1 (.D({32{1'b0}}), .en(o300), .Q(o00), .clk(in_1), .clr(in_2));
  Register #(.width(32)) register_2 (.D(in_7), .en(o308), .Q(o08), .clk(in_1), .clr(in_2));
  Register #(.width(32)) register_3 (.D(in_7), .en(o316), .Q(o16), .clk(in_1), .clr(in_2));
  Register #(.width(32)) register_4 (.D(in_7), .en(o324), .Q(o24), .clk(in_1), .clr(in_2));
  Register #(.width(32)) register_5 (.D(in_7), .en(o301), .Q(o01), .clk(in_1), .clr(in_2));
  Register #(.width(32)) register_6 (.D(in_7), .en(o309), .Q(o09), .clk(in_1), .clr(in_2));
  Register #(.width(32)) register_7 (.D(in_7), .en(o317), .Q(o17), .clk(in_1), .clr(in_2));
  Register #(.width(32)) register_8 (.D(in_7), .en(o325), .Q(o25), .clk(in_1), .clr(in_2));
  Register #(.width(32)) register_9 (.D(in_7), .en(o302), .Q(o02), .clk(in_1), .clr(in_2));
  Register #(.width(32)) register_10 (.D(in_7), .en(o310), .Q(o10), .clk(in_1), .clr(in_2));
  Register #(.width(32)) register_11 (.D(in_7), .en(o318), .Q(o18), .clk(in_1), .clr(in_2));
  Register #(.width(32)) register_12 (.D(in_7), .en(o326), .Q(o26), .clk(in_1), .clr(in_2));
  Register #(.width(32)) register_13 (.D(in_7), .en(o303), .Q(o03), .clk(in_1), .clr(in_2));
  Register #(.width(32)) register_14 (.D(in_7), .en(o311), .Q(o11), .clk(in_1), .clr(in_2));
  Multiplexer #(.select(5), .width(32), .enable("false")) multiplexer_1 (
    .in0(o00), .in1(o01), .in2(o02), .in3(o03), .in4(o04), .in5(o05), .in6(o06), .in7(o07), .in8(o08),
    .in9(o09), .in10(o10), .in11(o11), .in12(o12), .in13(o13), .in14(o14), .in15(o15), .in16(o16),
    .in17(o17), .in18(o18), .in19(o19), .in20(o20), .in21(o21), .in22(o22), .in23(o23), .in24(o24),
    .in25(o25), .in26(o26), .in27(o27), .in28(o28), .in29(o29), .in30(o30), .in31(o31), .out(out_8),
    .sel(in_4));
  Register #(.width(32)) register_15 (.D(in_7), .en(o319), .Q(o19), .clk(in_1), .clr(in_2));
  Register #(.width(32)) register_16 (.D(in_7), .en(o327), .Q(o27), .clk(in_1), .clr(in_2));
  Register #(.width(32)) register_17 (.D(in_7), .en(o304), .Q(o04), .clk(in_1), .clr(in_2));
  Register #(.width(32)) register_18 (.D(in_7), .en(o312), .Q(o12), .clk(in_1), .clr(in_2));
  Register #(.width(32)) register_19 (.D(in_7), .en(o320), .Q(o20), .clk(in_1), .clr(in_2));
  Register #(.width(32)) register_20 (.D(in_7), .en(o328), .Q(o28), .clk(in_1), .clr(in_2));
  Register #(.width(32)) register_21 (.D(in_7), .en(o305), .Q(o05), .clk(in_1), .clr(in_2));
  Register #(.width(32)) register_22 (.D(in_7), .en(o313), .Q(o13), .clk(in_1), .clr(in_2));
  Register #(.width(32)) register_23 (.D(in_7), .en(o321), .Q(o21), .clk(in_1), .clr(in_2));
  Register #(.width(32)) register_24 (.D(in_7), .en(o329), .Q(o29), .clk(in_1), .clr(in_2));
  Multiplexer #(.select(5), .width(32), .enable("false")) multiplexer_2 (
    .in0(o00), .in1(o01), .in2(o02), .in3(o03), .in4(o04), .in5(o05), .in6(o06), .in7(o07), .in8(o08),
    .in9(o09), .in10(o10), .in11(o11), .in12(o12), .in13(o13), .in14(o14), .in15(o15), .in16(o16),
    .in17(o17), .in18(o18), .in19(o19), .in20(o20), .in21(o21), .in22(o22), .in23(o23), .in24(o24),
    .in25(o25), .in26(o26), .in27(o27), .in28(o28), .in29(o29), .in30(o30), .in31(o31), .out(out_9),
    .sel(in_5));
  Register #(.width(32)) register_25 (.D(in_7), .en(o306), .Q(o06), .clk(in_1), .clr(in_2));
  Register #(.width(32)) register_26 (.D(in_7), .en(o314), .Q(o14), .clk(in_1), .clr(in_2));
  Register #(.width(32)) register_27 (.D(in_7), .en(o322), .Q(o22), .clk(in_1), .clr(in_2));
  Register #(.width(32)) register_28 (.D(in_7), .en(o330), .Q(o30), .clk(in_1), .clr(in_2));
  Register #(.width(32)) register_29 (.D(in_7), .en(o307), .Q(o07), .clk(in_1), .clr(in_2));
  Register #(.width(32)) register_30 (.D(in_7), .en(o315), .Q(o15), .clk(in_1), .clr(in_2));
  Register #(.width(32)) register_31 (.D(in_7), .en(o323), .Q(o23), .clk(in_1), .clr(in_2));
  Register #(.width(32)) register_32 (.D(in_7), .en(o331), .Q(o31), .clk(in_1), .clr(in_2));

  // Other names for the same wires on the sheet: A1[4:0] = in_4; A2[4:0] = in_5; A3[4:0] = in_6; clk = in_1;
  //   in[31:0] = in_7; reset = in_2; we = in_3
endmodule
