// Logisim project fib.circ as structural Verilog: 1 circuit, main circuit main
// for i=2;i<=n;i++
module main (
  input  [2:0] in_1,
  output [3:0] out_2
);

  wire Clear, clock_1_out, clock_2_out, clock_3_out, clock_4_out, Counter, GetFirstValue_q;
  wire [2:0] counter_1_q;
  wire [3:0] adder_1_out, FI_1, FI_2, multiplexer_1_out;

  Clock clock_1 (.out(clock_1_out));
  Adder #(.width(4)) adder_1 (.a(FI_1), .b(FI_2), .out(adder_1_out));  // open: cin, cout
  Clock clock_2 (.out(clock_2_out));
  Counter #(.width(3), .max('h7)) counter_1 (
    .count(Counter), .Q(counter_1_q), .clk(clock_1_out), .clr(Clear));  // open: load, D, carry
  Multiplexer #(.width(4), .enable("false")) multiplexer_1 (
    .in0(4'b0001), .in1(adder_1_out), .out(multiplexer_1_out), .sel(GetFirstValue_q));
  Register #(.width(1)) GetFirstValue (.D(Counter), .Q(GetFirstValue_q), .clk(clock_2_out), .clr(Clear));  // open: en
  Comparator #(.width(3), .mode("unsigned")) comparator_1 (.a(in_1), .b(counter_1_q), .gt(Counter));  // open: eq, lt
  // Probe on multiplexer_1_out
  Clock clock_3 (.out(clock_3_out));
  Multiplexer #(.width(4), .enable("false")) multiplexer_2 (.in0(FI_1), .in1(4'b0000), .out(out_2), .sel(Counter));
  Register #(.width(4)) f__i_1 (.D(multiplexer_1_out), .en(Counter), .Q(FI_1), .clk(clock_3_out), .clr(Clear));
  Clock clock_4 (.out(clock_4_out));
  Register #(.width(4)) f__i_2 (.D(FI_1), .en(Counter), .Q(FI_2), .clk(clock_4_out), .clr(Clear));
endmodule
