// Logisim project fib_int32.circ as structural Verilog: 2 circuits, main circuit main
module main (
  input  [31:0] Input,
  output [31:0] out_2
);

  wire and_1_out, Clear, clock_1_out, clock_2_out, clock_3_out, clock_4_out, clock_5_out, clock_6_out,
       clock_7_out, clock_8_out, clock_9_out, clock_10_out, clock_11_out, EnableMatrixMultyA_B, \end , init,
       not_1_out, or_1_out, register_1_q, spe, Unable;
  wire [31:0] a00, a01, a10, a11, b00, b01, b10, b11, divider_1_out, divider_1_rem, divider_2_rem, LastP,
       matrixmultiply_1_out_9, matrixmultiply_1_out_10, matrixmultiply_1_out_11, matrixmultiply_1_out_12,
       matrixmultiply_2_out_9, matrixmultiply_2_out_10, matrixmultiply_2_out_11, matrixmultiply_2_out_12,
       multiplexer_2_out, NowP, register_2_q, register_3_q, register_4_q, register_5_q, register_6_q,
       register_7_q, register_8_q, register_9_q;

  Clock clock_1 (.out(clock_1_out));
  Register #(.width(1)) initializer (.D(1'b1), .Q(init), .clk(clock_1_out), .clr(Clear));  // open: en
  Divider #(.width(32)) divider_1 (.a(NowP), .b(32'h2), .out(divider_1_out), .rem(divider_1_rem));  // open: upper
  Register #(.width(32)) register_P (.D(divider_1_out), .en(1'b1), .Q(LastP), .clk(clock_2_out), .clr(Clear));
  Clock clock_2 (.out(clock_2_out));
  Multiplexer #(.width(32), .enable("false")) multiplexer_1 (.in0(Input), .in1(LastP), .out(NowP), .sel(init));
  Divider #(.width(32)) divider_2 (.a(Input), .b(32'h2), .rem(divider_2_rem));  // open: out, upper
  Register #(.width(1)) register_1 (.D(\end ), .Q(register_1_q), .clk(clock_3_out), .clr(Clear));  // open: en
  Comparator #(.width(32), .mode("unsigned")) comparator_1 (.a({32{1'b0}}), .b(NowP), .eq(\end ));  // open: gt, lt
  Clock clock_3 (.out(clock_3_out));
  Comparator #(.width(32), .mode("unsigned")) comparator_2 (
    .a({32{1'b0}}), .b(divider_1_rem), .lt(EnableMatrixMultyA_B));  // open: gt, eq
  not not_1 (not_1_out, init);
  and and_1 (and_1_out, EnableMatrixMultyA_B, Unable);
  Comparator #(.width(32), .mode("unsigned")) comparator_3 (
    .a({32{1'b0}}), .b(divider_2_rem), .eq(spe));  // open: gt, lt
  // Probe on Input
  not not_2 (Unable, register_1_q);
  or or_1 (or_1_out, not_1_out, and_1_out, and_1_out);
  Register #(.width(32)) register_2 (.D(a00), .en(or_1_out), .Q(register_2_q), .clk(clock_4_out), .clr(Clear));
  Clock clock_4 (.out(clock_4_out));
  Register #(.width(32)) register_3 (.D(a01), .en(or_1_out), .Q(register_3_q), .clk(clock_5_out), .clr(Clear));
  Clock clock_5 (.out(clock_5_out));
  Register #(.width(32)) register_4 (.D(a10), .en(or_1_out), .Q(register_4_q), .clk(clock_6_out), .clr(Clear));
  Clock clock_6 (.out(clock_6_out));
  Register #(.width(32)) register_5 (.D(a11), .en(or_1_out), .Q(register_5_q), .clk(clock_7_out), .clr(Clear));
  Clock clock_7 (.out(clock_7_out));
  Register #(.width(32)) register_6 (.D(b00), .en(Unable), .Q(register_6_q), .clk(clock_8_out), .clr(Clear));
  Clock clock_8 (.out(clock_8_out));
  Register #(.width(32)) register_7 (.D(b01), .en(Unable), .Q(register_7_q), .clk(clock_9_out), .clr(Clear));
  Clock clock_9 (.out(clock_9_out));
  Register #(.width(32)) register_8 (.D(b10), .en(Unable), .Q(register_8_q), .clk(clock_10_out), .clr(Clear));
  Clock clock_10 (.out(clock_10_out));
  Register #(.width(32)) register_9 (.D(b11), .en(Unable), .Q(register_9_q), .clk(clock_11_out), .clr(Clear));
  Clock clock_11 (.out(clock_11_out));
  Multiplexer #(.width(32)) multiplexer_2 (
    .in0(register_2_q), .in1(register_3_q), .out(multiplexer_2_out), .sel(spe));  // open: en
  MatrixMultiply matrixmultiply_1 (
    .in_1(register_2_q), .in_2(register_3_q), .in_3(register_4_q), .in_4(register_5_q), .in_5(b00),
    .in_6(b01), .in_7(b10), .in_8(b11), .out_9(matrixmultiply_1_out_9), .out_10(matrixmultiply_1_out_10),
    .out_11(matrixmultiply_1_out_11), .out_12(matrixmultiply_1_out_12));
  MatrixMultiply matrixmultiply_2 (
    .in_1(register_6_q), .in_2(register_7_q), .in_3(register_8_q), .in_4(register_9_q), .in_5(register_6_q),
    .in_6(register_7_q), .in_7(register_8_q), .in_8(register_9_q), .out_9(matrixmultiply_2_out_9),
    .out_10(matrixmultiply_2_out_10), .out_11(matrixmultiply_2_out_11), .out_12(matrixmultiply_2_out_12));
  Multiplexer #(.width(32), .enable("false")) multiplexer_3 (
    .in0(32'h1), .in1(matrixmultiply_1_out_9), .out(a00), .sel(init));
  Multiplexer #(.width(32), .enable("false")) multiplexer_4 (
    .in0({32{1'b0}}), .in1(matrixmultiply_1_out_10), .out(a01), .sel(init));
  Multiplexer #(.width(32), .enable("false")) multiplexer_5 (
    .in0({32{1'b0}}), .in1(matrixmultiply_1_out_11), .out(a10), .sel(init));
  Multiplexer #(.width(32), .enable("false")) multiplexer_6 (
    .in0(32'h1), .in1(matrixmultiply_1_out_12), .out(a11), .sel(init));
  Multiplexer #(.width(32), .enable("false")) multiplexer_7 (
    .in0(32'h1), .in1(matrixmultiply_2_out_9), .out(b00), .sel(init));
  Multiplexer #(.width(32), .enable("false")) multiplexer_8 (
    .in0(32'h1), .in1(matrixmultiply_2_out_10), .out(b01), .sel(init));
  Multiplexer #(.width(32), .enable("false")) multiplexer_9 (
    .in0(32'h1), .in1(matrixmultiply_2_out_11), .out(b10), .sel(init));
  Multiplexer #(.width(32), .enable("false")) multiplexer_10 (
    .in0({32{1'b0}}), .in1(matrixmultiply_2_out_12), .out(b11), .sel(init));
  Multiplexer #(.width(32), .enable("false")) multiplexer_11 (
    .in0({32{1'b0}}), .in1(multiplexer_2_out), .out(out_2), .sel(\end ));
endmodule

module MatrixMultiply (
  input  [31:0] in_1,
  input  [31:0] in_2,
  input  [31:0] in_3,
  input  [31:0] in_4,
  input  [31:0] in_5,
  input  [31:0] in_6,
  input  [31:0] in_7,
  input  [31:0] in_8,
  output [31:0] out_9,
  output [31:0] out_10,
  output [31:0] out_11,
  output [31:0] out_12
);

  wire [31:0] multiplier_1_out, multiplier_2_out, multiplier_3_out, multiplier_4_out, multiplier_5_out,
       multiplier_6_out, multiplier_7_out, multiplier_8_out;

  Multiplier #(.width(32)) multiplier_1 (.a(in_1), .b(in_5), .out(multiplier_1_out));  // open: cin, cout
  Multiplier #(.width(32)) multiplier_2 (.a(in_2), .b(in_7), .out(multiplier_2_out));  // open: cin, cout
  Multiplier #(.width(32)) multiplier_3 (.a(in_1), .b(in_6), .out(multiplier_3_out));  // open: cin, cout
  Multiplier #(.width(32)) multiplier_4 (.a(in_2), .b(in_8), .out(multiplier_4_out));  // open: cin, cout
  Multiplier #(.width(32)) multiplier_5 (.a(in_3), .b(in_5), .out(multiplier_5_out));  // open: cin, cout
  Multiplier #(.width(32)) multiplier_6 (.a(in_4), .b(in_7), .out(multiplier_6_out));  // open: cin, cout
  Multiplier #(.width(32)) multiplier_7 (.a(in_3), .b(in_6), .out(multiplier_7_out));  // open: cin, cout
  Multiplier #(.width(32)) multiplier_8 (.a(in_4), .b(in_8), .out(multiplier_8_out));  // open: cin, cout
  Adder #(.width(32)) adder_1 (.a(multiplier_1_out), .b(multiplier_2_out), .out(out_9));  // open: cin, cout
  Adder #(.width(32)) adder_2 (.a(multiplier_3_out), .b(multiplier_4_out), .out(out_10));  // open: cin, cout
  Adder #(.width(32)) adder_3 (.a(multiplier_5_out), .b(multiplier_6_out), .out(out_11));  // open: cin, cout
  Adder #(.width(32)) adder_4 (.a(multiplier_7_out), .b(multiplier_8_out), .out(out_12));  // open: cin, cout

  // Other names for the same wires on the sheet: a00[31:0] = in_1; a01[31:0] = in_2; a10[31:0] = in_3;
  //   a11[31:0] = in_4; b00[31:0] = in_5; b01[31:0] = in_6; b10[31:0] = in_7; b11[31:0] = in_8
endmodule
