// Logisim project mod5.circ as structural Verilog
module mod5 (
  input  in_1,
  output out_2,
  output out_3,
  output out_4,
  output out_5,
  output out_6
);

  wire clock_1_out, S1, S2;
  wire [1:0] fsm_1_s1;

  fsm fsm_1 (.A(S1), .B(S2), .S(in_1), .S0(fsm_1_s1[1]), .S1(fsm_1_s1[0]));
  // Probe on fsm_1_s1
  // Probe on fsm_1_s1
  Register #(.width(2)) register_1 (.D(fsm_1_s1), .en(1'b1), .Q({S2, S1}), .clk(clock_1_out));  // open: clr
  // Probe on {S2, S1}
  Clock clock_1 (.out(clock_1_out));
  Decoder #(.select(2)) decoder_1 (.out0(out_3), .out1(out_4), .out2(out_5), .out3(out_6), .sel(fsm_1_s1));  // open: en

  assign out_2 = 1'b0;
endmodule

module fsm (
  input  A,
  input  B,
  input  S,
  output S0,
  output S1
);

  wire and_1_out, and_2_out, and_3_out, and_4_out, and_5_out, and_6_out, not_1_out, not_2_out, not_3_out,
       not_4_out, not_5_out, not_6_out, not_7_out, not_8_out;

  not not_1 (not_1_out, A);
  not not_2 (not_2_out, B);
  not not_3 (not_3_out, A);
  not not_4 (not_4_out, B);
  not not_5 (not_5_out, A);
  not not_6 (not_6_out, S);
  not not_7 (not_7_out, B);
  not not_8 (not_8_out, S);
  and and_1 (and_1_out, not_1_out, B);
  and and_2 (and_2_out, A, not_2_out);
  and and_3 (and_3_out, not_3_out, not_4_out, S);
  and and_4 (and_4_out, not_5_out, B, not_6_out);
  and and_5 (and_5_out, A, not_7_out, not_8_out);
  and and_6 (and_6_out, A, B, S);
  or or_1 (S0, and_1_out, and_2_out);
  or or_2 (S1, and_3_out, and_4_out, and_5_out, and_6_out);
endmodule
