// Logisim project sort.circ as structural Verilog
module _1bit_swap (
  input  A,
  input  B,
  input  C,
  output S,
  output T
);

  wire and_1_out, and_2_out, and_3_out, and_4_out, not_1_out, not_2_out;

  not not_1 (not_1_out, C);
  not not_2 (not_2_out, C);
  and and_1 (and_1_out, B, C);
  and and_2 (and_2_out, A, not_1_out);
  and and_3 (and_3_out, B, not_2_out);
  and and_4 (and_4_out, A, C);
  or or_1 (S, and_1_out, and_2_out);
  or or_2 (T, and_3_out, and_4_out);
endmodule

module _4bit_swap (
  input  [3:0] in_1,
  input  [3:0] in_2,
  input  in_3,
  output [3:0] out_4,
  output [3:0] out_5
);

  _1bit_swap u_1bit_swap_1 (.A(in_1[0]), .B(in_2[0]), .C(in_3), .S(out_4[0]), .T(out_5[0]));
  _1bit_swap u_1bit_swap_2 (.A(in_1[1]), .B(in_2[1]), .C(in_3), .S(out_4[1]), .T(out_5[1]));
  _1bit_swap u_1bit_swap_3 (.A(in_1[2]), .B(in_2[2]), .C(in_3), .S(out_4[2]), .T(out_5[2]));
  _1bit_swap u_1bit_swap_4 (.A(in_1[3]), .B(in_2[3]), .C(in_3), .S(out_4[3]), .T(out_5[3]));

  // Other names for the same wires on the sheet: C = in_3; a1_t = in_1[0]; a2_t = in_1[1]; a3_t = in_1[2];
  //   a4_t = in_1[3]; b1_t = in_2[0]; b2_t = in_2[1]; b3_t = in_2[2]; b4_t = in_2[3]; A1 = out_4[0]; A2 = out_4[1];
  //   A3 = out_4[2]; A4 = out_4[3]; B1 = out_5[0]; B2 = out_5[1]; B3 = out_5[2]; B4 = out_5[3]
endmodule

module _4bit_sort (
  input  [3:0] in_1,
  input  [3:0] in_2,
  input  [3:0] in_3,
  input  [3:0] in_4,
  output [3:0] out_5,
  output [3:0] out_6,
  output [3:0] out_7,
  output [3:0] out_8
);

  wire [3:0] bubble_sort_a_round_1_out_5, bubble_sort_a_round_1_out_6, bubble_sort_a_round_1_out_7,
       bubble_sort_a_round_1_out_8, bubble_sort_a_round_2_out_5, bubble_sort_a_round_2_out_6,
       bubble_sort_a_round_2_out_7, bubble_sort_a_round_2_out_8, bubble_sort_a_round_3_out_5,
       bubble_sort_a_round_3_out_6, bubble_sort_a_round_3_out_7, bubble_sort_a_round_3_out_8;

  bubble_sort_a_round bubble_sort_a_round_1 (
    .in_1(bubble_sort_a_round_2_out_5), .in_2(bubble_sort_a_round_2_out_6),
    .in_3(bubble_sort_a_round_2_out_7), .in_4(bubble_sort_a_round_2_out_8),
    .out_5(bubble_sort_a_round_1_out_5), .out_6(bubble_sort_a_round_1_out_6),
    .out_7(bubble_sort_a_round_1_out_7), .out_8(bubble_sort_a_round_1_out_8));
  bubble_sort_a_round bubble_sort_a_round_2 (
    .in_1(in_1), .in_2(in_2), .in_3(in_3), .in_4(in_4), .out_5(bubble_sort_a_round_2_out_5),
    .out_6(bubble_sort_a_round_2_out_6), .out_7(bubble_sort_a_round_2_out_7),
    .out_8(bubble_sort_a_round_2_out_8));
  bubble_sort_a_round bubble_sort_a_round_3 (
    .in_1(bubble_sort_a_round_1_out_5), .in_2(bubble_sort_a_round_1_out_6),
    .in_3(bubble_sort_a_round_1_out_7), .in_4(bubble_sort_a_round_1_out_8),
    .out_5(bubble_sort_a_round_3_out_5), .out_6(bubble_sort_a_round_3_out_6),
    .out_7(bubble_sort_a_round_3_out_7), .out_8(bubble_sort_a_round_3_out_8));
  bubble_sort_a_round bubble_sort_a_round_4 (
    .in_1(bubble_sort_a_round_3_out_5), .in_2(bubble_sort_a_round_3_out_6),
    .in_3(bubble_sort_a_round_3_out_7), .in_4(bubble_sort_a_round_3_out_8), .out_5(out_5), .out_6(out_6),
    .out_7(out_7), .out_8(out_8));
endmodule

module bubble_sort_a_round (
  input  [3:0] in_1,
  input  [3:0] in_2,
  input  [3:0] in_3,
  input  [3:0] in_4,
  output [3:0] out_5,
  output [3:0] out_6,
  output [3:0] out_7,
  output [3:0] out_8
);

  wire comparator_1_eq, comparator_1_gt, comparator_2_eq, comparator_2_gt, comparator_3_eq, comparator_3_gt,
       or_1_out, or_2_out, or_3_out;
  wire [3:0] n4bit_swap_1_out_5, n4bit_swap_2_out_5;

  Comparator #(.width(4), .mode("unsigned")) comparator_1 (
    .a(in_1), .b(in_2), .gt(comparator_1_gt), .eq(comparator_1_eq));  // open: lt
  Comparator #(.width(4), .mode("unsigned")) comparator_2 (
    .a(n4bit_swap_2_out_5), .b(in_4), .gt(comparator_2_gt), .eq(comparator_2_eq));  // open: lt
  or or_1 (or_1_out, comparator_1_gt, comparator_1_eq);
  Comparator #(.width(4), .mode("unsigned")) comparator_3 (
    .a(n4bit_swap_1_out_5), .b(in_3), .gt(comparator_3_gt), .eq(comparator_3_eq));  // open: lt
  _4bit_swap u_4bit_swap_1 (.in_1(in_1), .in_2(in_2), .in_3(or_1_out), .out_4(out_5), .out_5(n4bit_swap_1_out_5));
  or or_2 (or_2_out, comparator_3_gt, comparator_3_eq);
  or or_3 (or_3_out, comparator_2_gt, comparator_2_eq);
  _4bit_swap u_4bit_swap_2 (
    .in_1(n4bit_swap_1_out_5), .in_2(in_3), .in_3(or_2_out), .out_4(out_6), .out_5(n4bit_swap_2_out_5));
  _4bit_swap u_4bit_swap_3 (.in_1(n4bit_swap_2_out_5), .in_2(in_4), .in_3(or_3_out), .out_4(out_7), .out_5(out_8));
endmodule
